# Fritzing sketch PhonographEmulatorV2_fritzing_2021 (saved by Fritzing 0.9.8b)
circuit board: 9cm x 7cm
breadboards: 1

parts:
  U1 = ADTL082 - Dual JFET Input Op Amps [part_number=ADTL082]
  U1_1 = AnalogDevices_ADTL082ARZ_subpart1 [part_number=ADTL082]
  U1_2 = AnalogDevices_ADTL082ARZ_subpart2 [part_number=ADTL082]
  R1 = Resistor [tolerance=±5% resistance=10k power=0.25 package=THT]
  R2 = Resistor [tolerance=±5% resistance=10k power=0.25 package=THT]
  C1 = Electrolytic Capacitor [capacitance=47µF package="100 mil [THT, electrolytic]"]
  R3 = Resistor [tolerance=±5% resistance=1M power=0.25 package=THT]
  R4 = Resistor [tolerance=±5% resistance=10k power=0.25 package=THT]
  J1 = female pin header, 3 pins [form="♀ (female)"]
  C3 = Electrolytic Capacitor [capacitance=1µF package="100 mil [THT, electrolytic]"]
  C4 = Electrolytic Capacitor [capacitance=1µF package="100 mil [THT, electrolytic]"]
  J2 = female pin header, 3 pins [form="♀ (female)"]
  R5 = Resistor [tolerance=±5% resistance=220 power=0.25 package=THT]
  D1 = Rectifier Diode [part_number=1N4148 package="300 mil [THT]"]
  D2 = Rectifier Diode [part_number=1N4148 package="300 mil [THT]"]
  J3 = female pin header, 3 pins [form="♀ (female)"]
  R6 = Resistor [tolerance=±5% resistance=47k power=0.25 package=THT]
  D3 = Rectifier Diode [part_number=1N4148 package="300 mil [THT]"]
  D4 = Rectifier Diode [part_number=1N4148 package="300 mil [THT]"]
  R7 = Resistor [tolerance=±5% resistance=33k power=0.25 package=THT]
  J4 = female pin header, 2 pins [form="♀ (female)"]
  U2 = ADTL082 - Dual JFET Input Op Amps [part_number=ADTL082]
  U2_1 = AnalogDevices_ADTL082ARZ_subpart1 [part_number=ADTL082]
  U2_2 = AnalogDevices_ADTL082ARZ_subpart2 [part_number=ADTL082]
  J5 = female pin header, 2 pins [form="♀ (female)"]
  C5 = Electrolytic Capacitor [capacitance=47µF package="100 mil [THT, electrolytic]"]
  R8 = Resistor [tolerance=±5% resistance=220k power=0.25 package=THT]
  R9 = Resistor [tolerance=±5% resistance=100k power=0.25 package=THT]
  R11 = Resistor [tolerance=±5% resistance=100k power=0.25 package=THT]
  Q1 = NPN-Transistor [part_number=2n3904 package="TO92 [THT]"]
  Q2 = NPN-Transistor [part_number=2n3904 package="TO92 [THT]"]
  R12 = Resistor [tolerance=±5% resistance=47k power=0.25 package=THT]
  R13 = Resistor [tolerance=±5% resistance=220 power=0.25 package=THT]
  R14 = Resistor [tolerance=±5% resistance=4.7k power=0.25 package=THT]
  C7 = Electrolytic Capacitor [capacitance=1µF package="100 mil [THT, electrolytic]"]
  R15 = Resistor [tolerance=±5% resistance=220k power=0.25 package=THT]
  R16 = Resistor [tolerance=±5% resistance=68k power=0.25 package=THT]
  Q3 = NPN-Transistor [part_number=BC547 package="TO92 [THT]"]
  R17 = Resistor [tolerance=±5% resistance=2.2k power=0.25 package=THT]
  R18 = Resistor [tolerance=±5% resistance=4.7k power=0.25 package=THT]
  R19 = Resistor [tolerance=±5% resistance=470 power=0.25 package=THT]
  C8 = Electrolytic Capacitor [capacitance=1µF package="100 mil [THT, electrolytic]"]
  C9 = Electrolytic Capacitor [capacitance=1µF package="100 mil [THT, electrolytic]"]
  J6 = female pin header, 3 pins [form="♀ (female)"]
  IC1 = IC, DIP package, 8 pins [chip_label=LM311]
  R20 = Resistor [tolerance=±5% resistance=47k power=0.25 package=THT]
  D5 = Rectifier Diode [part_number=1N4148 package="300 mil [THT]"]
  R21 = Resistor [tolerance=±5% resistance=4.7k power=0.25 package=THT]
  J7 = female pin header, 3 pins [form="♀ (female)"]
  R23 = Resistor [tolerance=±5% resistance=5.6k power=0.25 package=THT]
  J8 = female pin header, 3 pins [form="♀ (female)"]
  IC2 = IC, DIP package, 14 pins [chip_label=4093]
  R24 = Resistor [tolerance=±5% resistance=22k power=0.25 package=THT]
  R25 = Resistor [tolerance=±5% resistance=1k power=0.25 package=THT]
  C12 = Electrolytic Capacitor [capacitance=1µF package="100 mil [THT, electrolytic]"]
  R26 = Resistor [tolerance=±5% resistance=56k power=0.25 package=THT]
  R27 = Resistor [tolerance=±5% resistance=22k power=0.25 package=THT]
  J9 = female pin header, 3 pins [form="♀ (female)"]
  C15 = Electrolytic Capacitor [capacitance=1µF package="100 mil [THT, electrolytic]"]
  R28 = Resistor [tolerance=±5% resistance=10k power=0.25 package=THT]
  J10 = female pin header, 3 pins [form="♀ (female)"]
  R29 = Resistor [tolerance=±5% resistance=10k power=0.25 package=THT]
  R30 = Resistor [tolerance=±5% resistance=10k power=0.25 package=THT]
  J11 = female pin header, 3 pins [form="♀ (female)"]
  R31 = Resistor [tolerance=±5% resistance=3.9k power=0.25 package=THT]
  R32 = Resistor [tolerance=±5% resistance=3.9k power=0.25 package=THT]
  J12 = female pin header, 3 pins [form="♀ (female)"]
  R33 = Resistor [tolerance=±5% resistance=1.8k power=0.25 package=THT]
  R34 = Resistor [tolerance=±5% resistance=1.8k power=0.25 package=THT]
  C20 = Electrolytic Capacitor [capacitance=1µF package="100 mil [THT, electrolytic]"]
  J13 = female pin header, 3 pins [form="♀ (female)"]
  J14 = female pin header, 2 pins [form="♀ (female)"]
  IC3 = Voltage Regulator [package=to-92]
  J15 = female pin header, 2 pins [form="♀ (female)"]
  D6 = Rectifier Diode [part_number=1N4001 package="300 mil [THT]"]
  R35 = Resistor [tolerance=±5% resistance=220 power=0.25 package=THT]
  LED1 = LED - 5mm [color="Red (633nm)" current=0.030 package="5 mm [THT]"]
  C2 = Ceramic Capacitor [capacitance=100nF package="200 mil [THT, multilayer]"]
  C6 = Ceramic Capacitor [capacitance=100nF package="200 mil [THT, multilayer]"]
  C18 = Ceramic Capacitor [capacitance=22nF package="200 mil [THT, multilayer]"]
  C19 = Ceramic Capacitor [capacitance=4.7nF package="200 mil [THT, multilayer]"]
  C16 = Ceramic Capacitor [capacitance=47nF package="200 mil [THT, multilayer]"]
  C17 = Ceramic Capacitor [capacitance=4.7nF package="200 mil [THT, multilayer]"]
  C10 = Ceramic Capacitor [capacitance=1nF package="200 mil [THT, multilayer]"]
  C11 = Ceramic Capacitor [capacitance=100nF package="200 mil [THT, multilayer]"]
  C13 = Ceramic Capacitor [capacitance=1nF package="200 mil [THT, multilayer]"]
  C14 = Ceramic Capacitor [capacitance=100nF package="200 mil [THT, multilayer]"]
  DPDT_Relay1 = DPDT Relay [chip_label=Relay package="DIP (Dual Inline) [THT]"]
  R36 = Resistor [tolerance=±5% resistance=220 power=0.25 package=THT]
  C22 = Ceramic Capacitor [capacitance=100nF package="200 mil [THT, multilayer]"]
  R10 = Resistor [tolerance=±5% resistance=220k power=0.25 package=THT]
  C24 = Electrolytic Capacitor [capacitance=1µF package="100 mil [THT, electrolytic]"]
  C23 = Ceramic Capacitor [capacitance=100pF package="200 mil [THT, multilayer]"]
  C25 = Ceramic Capacitor [capacitance=100nF package="200 mil [THT, multilayer]"]
  C26 = Ceramic Capacitor [capacitance=100nF voltage=35V package="200 mil [THT, multilayer]"]

nets:
  N1: U1.connector1, U1_1.connector1, J1.pin1, J1.pin2, C3.+
  N2: U1.connector2, U1_1.connector2, R4.Pin_1, J1.pin3
  N3: U1.connector3, U1_1.connector3, R3.Pin_1, C2.0
  GND: U1.connector4, U1_1.connector4, R2.Pin_0, C1.-, D1.cathode, D2.anode, J4.pin1, U2.connector4, U2_1.connector4, J5.pin1, C5.-, R13.Pin_0, R16.Pin_0, R17.Pin_0, C8.-, J6.pin3, IC1.pin1, IC1.pin4, IC1.pin7, D5.anode, R21.Pin_0, J7.pin1, R23.Pin_0, IC2.pin1, IC2.pin7, R25.Pin_0, J9.pin3, J14.pin2, IC3.GND, D6.anode, LED1.cathode, C10.0, C13.0, DPDT_Relay1.pin1, C22.0, C24.-
  N4: U1.connector5, U1_2.connector5, J3.pin1, D3.anode, D4.cathode, R7.Pin_1
  N5: U1.connector6, U1.connector7, U1_2.connector6, U1_2.connector7, C6.1
  12V: U1.connector8, U1_1.connector8, R1.Pin_1, U2.connector8, U2_1.connector8, J5.pin2, C5.+, IC1.pin8, R21.Pin_1, J7.pin3, IC2.pin14, IC3.IN, R36.Pin_0
  6V: R1.Pin_0, R2.Pin_1, C1.+, R3.Pin_0, R4.Pin_0, R7.Pin_0, U2.connector3, U2.connector5, U2_1.connector3, U2_2.connector5
  N6: C3.-, J2.pin1, J13.pin1
  N7: C4.-, J3.pin3, R6.Pin_0
  N8: C4.+, J2.pin3
  N9: J2.pin2, R5.Pin_1
  N10: R5.Pin_0, D1.anode, D2.cathode
  N11: J3.pin2, R6.Pin_1, D3.cathode, D4.anode
  N12: J4.pin2, DPDT_Relay1.pin2
  N13: U2.connector1, U2_1.connector1, R9.Pin_1, C15.+, C23.0
  N14: U2.connector2, U2_1.connector2, R8.Pin_1, R9.Pin_0, R11.Pin_1, R10.Pin_1, C23.1
  N15: U2.connector6, U2_2.connector6, R30.Pin_1, C18.0, C19.0
  N16: U2.connector7, U2_2.connector7, R29.Pin_1, R31.Pin_1, R34.Pin_1, C20.+
  N17: R8.Pin_0, C6.0
  N18: R11.Pin_0, C26.1
  N19: Q1.E, R13.Pin_1
  N20: Q1.B, Q2.B
  N21: Q1.C, R12.Pin_1, R14.Pin_0, C7.+
  N22: Q2.E, R12.Pin_0, C24.+
  N23: R14.Pin_1, R15.Pin_1, R18.Pin_1, R36.Pin_1, C22.1
  N24: C7.-, R15.Pin_0, R16.Pin_1, Q3.B
  N25: Q3.E, R17.Pin_1, R19.Pin_0
  N26: Q3.C, R18.Pin_0, C9.+, R20.Pin_0
  N27: R19.Pin_1, C8.+
  N28: C9.-, J6.pin1
  N29: J6.pin2, C25.1
  N30: IC1.pin2, R20.Pin_1, D5.cathode
  N31: IC1.pin3, J8.pin2
  N32: J7.pin2, J8.pin3
  N33: R23.Pin_1, J8.pin1
  N34: IC2.pin2, IC2.pin4, R24.Pin_0
  N35: IC2.pin3, IC2.pin8, C11.1
  N36: IC2.pin5, IC2.pin6, R24.Pin_1, C10.1
  N37: IC2.pin9, R25.Pin_1, C11.0
  N38: IC2.pin10, IC2.pin12, IC2.pin13
  N39: IC2.pin11, C12.+
  N40: C12.-, R26.Pin_0
  N41: R26.Pin_1, C13.1, C14.1
  N42: R27.Pin_0, C14.0
  N43: R27.Pin_1, J9.pin1
  N44: J9.pin2, C26.0
  N45: C15.-, R28.Pin_0, R32.Pin_0, R33.Pin_0
  N46: R28.Pin_1, J10.pin1, C16.1
  N47: J10.pin2, R30.Pin_0
  N48: J10.pin3, R29.Pin_0, C16.0
  N49: J11.pin1, R32.Pin_1, C17.1
  N50: J11.pin2, C18.1
  N51: J11.pin3, R31.Pin_0, C17.0
  N52: J12.pin1, R33.Pin_1
  N53: J12.pin2, C19.1
  N54: J12.pin3, R34.Pin_0
  N55: C20.-, J13.pin3
  N56: J13.pin2, DPDT_Relay1.pin6
  N57: J14.pin1, DPDT_Relay1.pin7
  N58: IC3.OUT, J15.pin1, D6.cathode
  N59: J15.pin2, R35.Pin_0, DPDT_Relay1.pin8
  N60: R35.Pin_1, LED1.anode
  N61: C2.1, DPDT_Relay1.pin3
  N62: DPDT_Relay1.pin4, DPDT_Relay1.pin5
  N63: R10.Pin_0, C25.0

notes:
  GAIN
  SATURATION
  10KB
  100KB
  CROSSOVER
  IN
  POWER IN
  HISS
  10KA
  Rand Adj. 10k trim
  RANDOMNESS
  CLIP
  500KB
  BASS
  MIDS
  TREBLE
  OUT
  Phonograph & Tape Emulator, Ernesto Gigliotti 2018. ernestogigliotti@gmail.com, 1.0
  BLEND
  FOOTSWITCH
  PHONOGRAPH
  EMULATOR

custom parts:
  DPDT Relay: DIP DPDT Relay (Double Pole Double Throw)
